# Fritzing sketch Alan_prot_01 (saved by Fritzing 0.9.3b)
breadboards: 4

parts:
  MUX1 = 74HC4051 [package="DIP (Dual Inline) [THT]"]
  Q1 = Basic FET N-Channel [part_number=IRLZ44 package="TO220 [THT]"]
  BATT-A = 18650 battery holder [package=battery-18650-kit]
  BATT-B = 18650 battery holder [package=battery-18650-kit]
  U2 = SWITCH_SPDT [package=kps-1290]
  U3 = SWITCH_SPDT [package=kps-1290]
  Skib01 = female pin header, 2 pins [form="♀ (female)"]
  R2 = Resistor [tolerance=±5% resistance=22k package=THT]
  MUX2 = 74HC4051 [package="DIP (Dual Inline) [THT]"]
  SR3 = 74HC595 [package="DIP16 [THT]"]
  R3 = Resistor [tolerance=±5% resistance=22k package=THT]
  C3 = Ceramic Capacitor [capacitance=100nF package="100 mil [THT, multilayer]"]
  C4 = Ceramic Capacitor [capacitance=100nF package="100 mil [THT, multilayer]"]
  ESP32_LORA = IC, DIP package, 36 pins [chip_label=ESP32]
  SR2 = 74HC595 [package="DIP16 [THT]"]
  SR1 = 74HC595 [package="DIP16 [THT]"]
  C1 = Ceramic Capacitor [capacitance=100nF package="100 mil [THT, multilayer]"]
  C2 = Ceramic Capacitor [capacitance=100nF package="100 mil [THT, multilayer]"]
  R7 = Resistor [tolerance=±5% resistance=1k package=THT]
  LTV1 = LTV847 [part_number=TLP521 package="DIP (Dual Inline) [THT]"]
  R8 = Resistor [tolerance=±5% resistance=22k package=THT]

nets:
  senSkib05: MUX1.IO4
  senSkib07: MUX1.IO6
  senseSkibs: MUX1.IO, MUX2.IO, ESP32_LORA.pin33
  senSkib08: MUX1.IO7
  senSkib06: MUX1.IO5
  sr3_q3: MUX1.INH, SR3.Q3
  GND/opt15: MUX1.VEE, MUX1.VSS, Q1.source, BATT-A.-, BATT-B.-, MUX2.VEE, MUX2.VSS, SR3.GND, SR3.OE, R3.Pin_0, C3.0, C4.0, ESP32_LORA.pin1, ESP32_LORA.pin4, ESP32_LORA.pin36, SR2.GND, SR2.OE, SR1.GND, SR1.OE, C1.0, C2.0, R7.Pin_0, LTV1.pin15
  sr3_q2: MUX1.C, MUX2.C, SR3.Q2
  sr3_q1: MUX1.B, MUX2.B, SR3.Q1
  sr3_q0: MUX1.A, MUX2.A, SR3.Q0
  senSkib04: MUX1.IO3
  opt16/senSkib01: MUX1.IO0, LTV1.pin16, R8.Pin_0
  senSkib02: MUX1.IO1
  senSkib03: MUX1.IO2
  3.3V: MUX1.VDD, MUX2.VDD, SR3.MR, SR3.VCC, C3.1, C4.1, ESP32_LORA.pin3, SR2.MR, SR2.VCC, SR1.MR, SR1.VCC, C1.1, C2.1, R8.Pin_1
  m01: Q1.gate, R3.Pin_1, SR1.Q0
  opt01: Q1.drain, Skib01.pin2, R2.Pin_0, LTV1.pin1
  N1: BATT-A.+, U3.P
  N2: BATT-B.+, U2.P
  vcc_Bat_B: U2.S, Skib01.pin1, R2.Pin_1
  vcc_Bat_A: U3.S
  senSkib13: MUX2.IO4
  senSkib15: MUX2.IO6
  senSkib16: MUX2.IO7
  senSkib14: MUX2.IO5
  sr3_q4: MUX2.INH, SR3.Q4
  senSkib12: MUX2.IO3
  senSkib09: MUX2.IO0
  senSkib10: MUX2.IO1
  senSkib11: MUX2.IO2
  sr3_q5: SR3.Q5
  sr3_q6: SR3.Q6
  sr3_q7: SR3.Q7
  sr3_clock: SR3.SH_CP, ESP32_LORA.pin26
  sr3_latch: SR3.ST_CP, ESP32_LORA.pin27
  sr3_data: SR3.DS, ESP32_LORA.pin25
  buzzer: ESP32_LORA.pin9
  sr_data: ESP32_LORA.pin19, SR1.DS
  sr_clock: ESP32_LORA.pin20, SR2.SH_CP, SR1.SH_CP
  sr_latch: ESP32_LORA.pin21, SR2.ST_CP, SR1.ST_CP
  m10: SR2.Q1
  m11: SR2.Q2
  m12: SR2.Q3
  m13: SR2.Q4
  m14: SR2.Q5
  m15: SR2.Q6
  m16: SR2.Q7
  N3: SR2.DS, SR1.Q7'
  m09: SR2.Q0
  m02: SR1.Q1
  m03: SR1.Q2
  m04: SR1.Q3
  m05: SR1.Q4
  m06: SR1.Q5
  m07: SR1.Q6
  m08: SR1.Q7
  opt02: R7.Pin_1, LTV1.pin2
  opt03: LTV1.pin3
  opt04: LTV1.pin4
  opt05: LTV1.pin5
  opt06: LTV1.pin6
  opt07: LTV1.pin7
  opt08: LTV1.pin8
  opt09: LTV1.pin9
  opt10: LTV1.pin10
  opt11: LTV1.pin11
  opt12: LTV1.pin12
  opt13: LTV1.pin13
  opt14: LTV1.pin14

notes:
  Mosfet Triggers
  https://www.codeproject.com/Articles/144606/Arduino-Platform-Working-with-Shift-Registers
  Batteries
  A
  B
  A (main)
  B (skibs)
  Skibs Sensors
  Microcontroller

custom parts:
  74HC4051: 8 channel analog multiplexer/demultiplexer
  18650 battery holder: 18650 Battery Holder
  LTV847: 4 opto-couplers
